# Fritzing sketch DS32KHz_Clock_stripboard (saved by Fritzing 0.9.2b)
circuit board: 10.5cm x 3.5cm
stripboards: 1

parts:
  R7 = Resistor [tolerance=±5% resistance=220 package="2010 [SMD]"]
  R8 = Resistor [tolerance=±5% resistance=220 package="2010 [SMD]"]
  R9 = Resistor [tolerance=±5% resistance=220 package="2010 [SMD]"]
  R10 = Resistor [tolerance=±5% resistance=220 package="2010 [SMD]"]
  R11 = Resistor [tolerance=±5% resistance=220 package="2010 [SMD]"]
  R12 = Resistor [tolerance=±5% resistance=220 package="2010 [SMD]"]
  R13 = Resistor [tolerance=±5% resistance=220 package="2010 [SMD]"]
  R14 = Resistor [tolerance=±5% resistance=220 package="2010 [SMD]"]
  IC1 = IC, DIP package, 28 pins [chip_label=PIC16F72]
  Q1 = NPN-Transistor [part_number=2N3904 package="TO92 [THT]"]
  Q2 = NPN-Transistor [part_number=2N3904 package="TO92 [THT]"]
  R16 = Resistor [tolerance=±5% resistance=220 package="2010 [SMD]"]
  C2 = Ceramic Capacitor [capacitance=33pF package="100 mil [THT, multilayer]"]
  IC2 = IC, DIP package, 14 pins [chip_label=DS32KHZ]
  C1 = Ceramic Capacitor [capacitance=33pF package="100 mil [THT, multilayer]"]
  JP1 = Header 6 [package=1x06_smd_straight_alt]
  JP2 = Header 6 [package=1x06_smd_straight_alt]
  JP3 = Header 6 [package=1x06_smd_straight_alt]
  R5 = Resistor [tolerance=±5% resistance=220 package="2010 [SMD]"]
  R4 = Resistor [tolerance=±5% resistance=220 package="2010 [SMD]"]
  R3 = Resistor [tolerance=±5% resistance=220 package="2010 [SMD]"]
  R2 = Resistor [tolerance=±5% resistance=220 package="2010 [SMD]"]
  R18 = Resistor [tolerance=±5% resistance=220 package="2010 [SMD]"]
  R1 = Resistor [tolerance=±5% resistance=220 package="2010 [SMD]"]
  R19 = Resistor [tolerance=±5% resistance=10k package="2010 [SMD]"]
  R6 = Resistor [tolerance=±5% resistance=220 package="2010 [SMD]"]
  Y1 = CRYSTAL [package=hc49u-v]
  X1 = USB Connectors [package=usb-microb]
  S1 = Pushbutton [package="[THT]"]
  R20 = Resistor [tolerance=±5% resistance=10k package=THT]

nets:
  N1: R7.Pin_0, IC1.pin28
  N2: R7.Pin_1, JP2.3
  N3: R8.Pin_0, IC1.pin27
  N4: R8.Pin_1, JP2.4
  N5: R9.Pin_0, IC1.pin26
  N6: R9.Pin_1, JP2.5
  N7: R10.Pin_0, IC1.pin25
  N8: R10.Pin_1, JP2.6
  N9: R11.Pin_0, IC1.pin24
  N10: R11.Pin_1, JP3.1
  N11: R12.Pin_0, IC1.pin23
  N12: R12.Pin_1, JP3.2
  N13: R13.Pin_0, IC1.pin22
  N14: R13.Pin_1, JP3.3
  N15: R14.Pin_0, IC1.pin21
  N16: R14.Pin_1, JP3.4
  RST: IC1.pin1, R19.Pin_1
  N17: IC1.pin3, R5.Pin_0
  N18: IC1.pin4, R4.Pin_0
  N19: IC1.pin5, R3.Pin_0
  N20: IC1.pin6, R2.Pin_0
  N21: IC1.pin7, R1.Pin_0
  GND: IC1.pin8, IC1.pin19, Q1.E, Q2.E, C2.1, IC2.pin4, IC2.pin5, C1.1, X1.GND, S1.Pin_3, S1.Pin_4
  N22: IC1.pin9, C1.0, Y1.1
  N23: IC1.pin10, C2.0, Y1.2
  N24: IC1.pin11, IC2.pin12
  N25: IC1.pin13, S1.Pin_1, S1.Pin_2, R20.Pin_0
  RC3: IC1.pin14, R6.Pin_0
  N26: IC1.pin15, R16.Pin_0
  N27: IC1.pin16, R18.Pin_0
  5V/Vcc: IC1.pin20, IC2.pin13, R19.Pin_0, X1.VBUS, R20.Pin_1
  N28: Q1.B, Q1.C, R16.Pin_1, JP3.6
  N29: Q2.B, R18.Pin_1
  N30: Q2.C, JP3.5
  N31: JP1.3, R1.Pin_1
  N32: JP1.4, R2.Pin_1
  N33: JP1.5, R3.Pin_1
  N34: JP1.6, R4.Pin_1
  N35: JP2.1, R5.Pin_1
  N36: JP2.2, R6.Pin_1
